// Logisim project Four_Bits_Add_Sub.circ as structural Verilog: 2 circuits, main circuit Add_Sub_4Bits
module Add_Sub_4Bits (
  input  [3:0] B,
  input  Add_Sub,
  input  [3:0] A,
  output [3:0] R,
  output Zero,
  output Overflow
);

  wire add_1bit_1_cout, add_1bit_2_cout, add_1bit_3_cout, add_1bit_4_cout, and_1_out, and_2_out, not_1_out,
       not_2_out, not_3_out, not_4_out, not_5_out, not_6_out, xnor_1_out, xnor_2_out, xnor_3_out, xnor_4_out;

  // Probe on A
  xnor xnor_1 (xnor_1_out, B[3], not_1_out);
  // Probe on B
  xnor xnor_2 (xnor_2_out, B[1], not_1_out);
  xnor xnor_3 (xnor_3_out, B[2], not_1_out);
  Add_1Bit add_1bit_1 (.Cout(add_1bit_1_cout), .Sum(R[3]), .Cin(add_1bit_4_cout), .A(xnor_1_out), .B(A[3]));
  xnor xnor_4 (xnor_4_out, B[0], not_1_out);
  Add_1Bit add_1bit_2 (.Cout(add_1bit_2_cout), .Sum(R[0]), .Cin(not_2_out), .A(xnor_4_out), .B(A[0]));
  Add_1Bit add_1bit_3 (.Cout(add_1bit_3_cout), .Sum(R[1]), .Cin(add_1bit_2_cout), .A(xnor_2_out), .B(A[1]));
  Add_1Bit add_1bit_4 (.Cout(add_1bit_4_cout), .Sum(R[2]), .Cin(add_1bit_3_cout), .A(xnor_3_out), .B(A[2]));
  not not_1 (not_1_out, Add_Sub);
  not not_2 (not_2_out, not_1_out);
  // Probe on R
  not not_3 (not_3_out, R[0]);
  not not_4 (not_4_out, R[1]);
  not not_5 (not_5_out, R[2]);
  and and_1 (and_1_out, not_3_out, not_4_out);
  and and_2 (and_2_out, not_5_out, not_6_out);
  not not_6 (not_6_out, R[3]);
  xor xor_1 (Overflow, add_1bit_4_cout, add_1bit_1_cout);
  and and_3 (Zero, and_1_out, and_2_out);

  // Notes on the sheet:
  //   YOUR NAME AND STUDENT NUMBER HERE
  //   Ken Li 260823059
  //   MAKE SURE THAT YOU OPEN THIS PROJECT IN "LOGISIM-EVOLUTION"
endmodule

module Add_1Bit (
  input  Cin,
  input  A,
  input  B,
  output Sum,
  output Cout
);

  wire and_1_out, and_2_out, xor_1_out;

  xor xor_1 (xor_1_out, A, B);
  and and_1 (and_1_out, xor_1_out, Cin);
  xor xor_2 (Sum, Cin, xor_1_out);
  and and_2 (and_2_out, A, B);
  or or_1 (Cout, and_1_out, and_2_out);

  // Notes on the sheet:
  //   YOUR NAME AND STUDENT NUMBER HERE
  //   Ken Li 260823059
  //   MAKE SURE THAT YOU OPENED THIS PROJECT IN "LOGISIM-EVOLUTION"
endmodule
