// Logisim project Ken_Li_260823059_FSM_logisim_evolution.circ as structural Verilog: 1 circuit, main circuit main
module main (
  input  DATA,
  input  RESET,
  output Z
);

  wire clock_1_out, d_ff_16_q;
  wire [1:0] divider_1_rem_2, divider_1_rem_3;
  wire [2:0] adder_1_out, d_ff_17_q, divider_1_rem_5;
  wire [4:0] divider_1_rem;
  wire [15:0] divider_1_out;
  wire [15:1] d_ff_1_q;
  wire [15:12] divider_1_rem_4;

  Clock clock_1 (.out(clock_1_out));
  D_Flip_Flop d_ff_1 (.D(DATA), .clk(clock_1_out), .Q(d_ff_1_q[1]), .preset(1'b0), .reset(RESET));  // open: Qn
  D_Flip_Flop d_ff_2 (.D(d_ff_1_q[1]), .clk(clock_1_out), .Q(d_ff_1_q[2]), .preset(1'b0), .reset(RESET));  // open: Qn
  D_Flip_Flop d_ff_3 (.D(d_ff_1_q[2]), .clk(clock_1_out), .Q(d_ff_1_q[3]), .preset(1'b0), .reset(RESET));  // open: Qn
  D_Flip_Flop d_ff_4 (.D(d_ff_1_q[3]), .clk(clock_1_out), .Q(d_ff_1_q[4]), .preset(1'b0), .reset(RESET));  // open: Qn
  D_Flip_Flop d_ff_5 (.D(d_ff_1_q[4]), .clk(clock_1_out), .Q(d_ff_1_q[5]), .preset(1'b0), .reset(RESET));  // open: Qn
  D_Flip_Flop d_ff_6 (.D(d_ff_1_q[5]), .clk(clock_1_out), .Q(d_ff_1_q[6]), .preset(1'b0), .reset(RESET));  // open: Qn
  D_Flip_Flop d_ff_7 (.D(d_ff_1_q[6]), .clk(clock_1_out), .Q(d_ff_1_q[7]), .preset(1'b0), .reset(RESET));  // open: Qn
  D_Flip_Flop d_ff_8 (.D(d_ff_1_q[7]), .clk(clock_1_out), .Q(d_ff_1_q[8]), .preset(1'b0), .reset(RESET));  // open: Qn
  D_Flip_Flop d_ff_9 (.D(d_ff_1_q[8]), .clk(clock_1_out), .Q(d_ff_1_q[9]), .preset(1'b0), .reset(RESET));  // open: Qn
  D_Flip_Flop d_ff_10 (.D(d_ff_1_q[9]), .clk(clock_1_out), .Q(d_ff_1_q[10]), .preset(1'b0), .reset(RESET));  // open: Qn
  D_Flip_Flop d_ff_11 (
    .D(d_ff_1_q[10]), .clk(clock_1_out), .Q(d_ff_1_q[11]), .preset(1'b0), .reset(RESET));  // open: Qn
  D_Flip_Flop d_ff_12 (
    .D(d_ff_1_q[11]), .clk(clock_1_out), .Q(d_ff_1_q[12]), .preset(1'b0), .reset(RESET));  // open: Qn
  D_Flip_Flop d_ff_13 (
    .D(d_ff_1_q[12]), .clk(clock_1_out), .Q(d_ff_1_q[13]), .preset(1'b0), .reset(RESET));  // open: Qn
  D_Flip_Flop d_ff_14 (
    .D(d_ff_1_q[13]), .clk(clock_1_out), .Q(d_ff_1_q[14]), .preset(1'b0), .reset(RESET));  // open: Qn
  D_Flip_Flop d_ff_15 (
    .D(d_ff_1_q[14]), .clk(clock_1_out), .Q(d_ff_1_q[15]), .preset(1'b0), .reset(RESET));  // open: Qn
  D_Flip_Flop d_ff_16 (.D(d_ff_1_q[15]), .clk(clock_1_out), .Q(d_ff_16_q), .preset(1'b0), .reset(RESET));  // open: Qn
  Divider #(.width(16)) divider_1 (
    .a({d_ff_1_q, DATA}), .b(16'h5), .out(divider_1_out), .upper({16{1'b0}}),
    .rem({divider_1_rem_4, divider_1_rem_3, divider_1_rem_2, divider_1_rem, divider_1_rem_5}));
  D_Flip_Flop d_ff_17 (.D(divider_1_rem_5[0]), .clk(clock_1_out), .Q(d_ff_17_q[0]));  // open: Qn, preset, reset
  D_Flip_Flop d_ff_18 (.D(divider_1_rem_5[1]), .clk(clock_1_out), .Q(d_ff_17_q[1]));  // open: Qn, preset, reset
  D_Flip_Flop d_ff_19 (.D(divider_1_rem_5[2]), .clk(clock_1_out), .Q(d_ff_17_q[2]));  // open: Qn, preset, reset
  Adder #(.width(3)) adder_1 (.a(d_ff_17_q), .b(divider_1_rem_5), .out(adder_1_out));  // open: cin, cout
  Comparator #(.width(3)) comparator_1 (.a(adder_1_out), .b(3'b000), .eq(Z));  // open: gt, lt
endmodule
