// Logisim project RAM_16_Nibbles_Read_Write.circ as structural Verilog: 5 circuits, main circuit RAM_16_Nibbles
// Clk
module RAM_16_Nibbles (
  input  [3:0] Data,
  input  Read_Write,
  input  [3:0] Address,
  output [3:0] RAM_OUT
);

  wire _0_3_out, _1_3_out, _2_3_out, _3_2_out, _4_2_out, _5_2_out, _6_2_out, _7_2_out, _8_2_out, _9_2_out,
       _10_2_out, _11_2_out, _12_2_out, _13_2_out, _14_2_out, _15_2_out, Clk_out, new_decoder_1_y0,
       new_decoder_1_y1, new_decoder_1_y2, new_decoder_1_y3, new_decoder_1_y4, new_decoder_1_y5,
       new_decoder_1_y6, new_decoder_1_y7, new_decoder_1_y8, new_decoder_1_y9, new_decoder_1_y10,
       new_decoder_1_y11, new_decoder_1_y12, new_decoder_1_y13, new_decoder_1_y14, new_decoder_1_y15;
  wire [3:0] _0_nibble_out, _1_nibble_out, _2_nibble_out, _3_nibble_out, _4_nibble_out, _5_nibble_out,
       _6_nibble_out, _7_nibble_out, _8_nibble_out, _9_nibble_out, _10_nibble_out, _11_nibble_out,
       _12_nibble_out, _13_nibble_out, _14_nibble_out, _15_nibble_out;

  // Probe on Data
  Nibble _3 (.Data(Data), .Read_Write(Read_Write), .Enable(_3_2_out), .Clk(Clk_out), .Nibble_Out(_3_nibble_out));
  Nibble _7 (.Data(Data), .Read_Write(Read_Write), .Enable(_7_2_out), .Clk(Clk_out), .Nibble_Out(_7_nibble_out));
  Nibble _11 (.Data(Data), .Read_Write(Read_Write), .Enable(_11_2_out), .Clk(Clk_out), .Nibble_Out(_11_nibble_out));
  Nibble _15 (.Data(Data), .Read_Write(Read_Write), .Enable(_15_2_out), .Clk(Clk_out), .Nibble_Out(_15_nibble_out));
  Nibble _2 (.Data(Data), .Read_Write(Read_Write), .Enable(_2_3_out), .Clk(Clk_out), .Nibble_Out(_2_nibble_out));
  Nibble _6 (.Data(Data), .Read_Write(Read_Write), .Enable(_6_2_out), .Clk(Clk_out), .Nibble_Out(_6_nibble_out));
  Nibble _10 (.Data(Data), .Read_Write(Read_Write), .Enable(_10_2_out), .Clk(Clk_out), .Nibble_Out(_10_nibble_out));
  Nibble _14 (.Data(Data), .Read_Write(Read_Write), .Enable(_14_2_out), .Clk(Clk_out), .Nibble_Out(_14_nibble_out));
  Clock Clk (.out(Clk_out));
  Nibble _1 (.Data(Data), .Read_Write(Read_Write), .Enable(_1_3_out), .Clk(Clk_out), .Nibble_Out(_1_nibble_out));
  Nibble _5 (.Data(Data), .Read_Write(Read_Write), .Enable(_5_2_out), .Clk(Clk_out), .Nibble_Out(_5_nibble_out));
  Nibble _9 (.Data(Data), .Read_Write(Read_Write), .Enable(_9_2_out), .Clk(Clk_out), .Nibble_Out(_9_nibble_out));
  Nibble _13 (.Data(Data), .Read_Write(Read_Write), .Enable(_13_2_out), .Clk(Clk_out), .Nibble_Out(_13_nibble_out));
  Nibble _0 (.Data(Data), .Read_Write(Read_Write), .Enable(_0_3_out), .Clk(Clk_out), .Nibble_Out(_0_nibble_out));
  Nibble _4 (.Data(Data), .Read_Write(Read_Write), .Enable(_4_2_out), .Clk(Clk_out), .Nibble_Out(_4_nibble_out));
  Nibble _8 (.Data(Data), .Read_Write(Read_Write), .Enable(_8_2_out), .Clk(Clk_out), .Nibble_Out(_8_nibble_out));
  Nibble _12 (.Data(Data), .Read_Write(Read_Write), .Enable(_12_2_out), .Clk(Clk_out), .Nibble_Out(_12_nibble_out));
  // Probe on Address
  _16_to_1_mux _1_2 (
    .D0(_0_nibble_out[1]), .D1(_1_nibble_out[1]), .D2(_2_nibble_out[1]), .D3(_3_nibble_out[1]),
    .D4(_4_nibble_out[1]), .D5(_5_nibble_out[1]), .D6(_6_nibble_out[1]), .D7(_7_nibble_out[1]),
    .D8(_8_nibble_out[1]), .D9(_9_nibble_out[1]), .D10(_10_nibble_out[1]), .D11(_11_nibble_out[1]),
    .D12(_12_nibble_out[1]), .D13(_13_nibble_out[1]), .D14(_14_nibble_out[1]), .D15(_15_nibble_out[1]),
    .A0(Address[0]), .A1(Address[1]), .A2(Address[2]), .A3(Address[3]), .out_21(RAM_OUT[1]));
  New_decoder new_decoder_1 (
    .A(Address[3]), .B(Address[2]), .C(Address[1]), .D(Address[0]), .Y0(new_decoder_1_y0),
    .Y1(new_decoder_1_y1), .Y2(new_decoder_1_y2), .Y3(new_decoder_1_y3), .Y4(new_decoder_1_y4),
    .Y5(new_decoder_1_y5), .Y6(new_decoder_1_y6), .Y7(new_decoder_1_y7), .Y8(new_decoder_1_y8),
    .Y9(new_decoder_1_y9), .Y10(new_decoder_1_y10), .Y11(new_decoder_1_y11), .Y12(new_decoder_1_y12),
    .Y13(new_decoder_1_y13), .Y14(new_decoder_1_y14), .Y15(new_decoder_1_y15));
  _16_to_1_mux _0_2 (
    .D0(_0_nibble_out[0]), .D1(_1_nibble_out[0]), .D2(_2_nibble_out[0]), .D3(_3_nibble_out[0]),
    .D4(_4_nibble_out[0]), .D5(_5_nibble_out[0]), .D6(_6_nibble_out[0]), .D7(_7_nibble_out[0]),
    .D8(_8_nibble_out[0]), .D9(_9_nibble_out[0]), .D10(_10_nibble_out[0]), .D11(_11_nibble_out[0]),
    .D12(_12_nibble_out[0]), .D13(_13_nibble_out[0]), .D14(_14_nibble_out[0]), .D15(_15_nibble_out[0]),
    .A0(Address[0]), .A1(Address[1]), .A2(Address[2]), .A3(Address[3]), .out_21(RAM_OUT[0]));
  and _0_3 (_0_3_out, Read_Write, new_decoder_1_y0);
  _16_to_1_mux _2_2 (
    .D0(_0_nibble_out[2]), .D1(_1_nibble_out[2]), .D2(_2_nibble_out[2]), .D3(_3_nibble_out[2]),
    .D4(_4_nibble_out[2]), .D5(_5_nibble_out[2]), .D6(_6_nibble_out[2]), .D7(_7_nibble_out[2]),
    .D8(_8_nibble_out[2]), .D9(_9_nibble_out[2]), .D10(_10_nibble_out[2]), .D11(_11_nibble_out[2]),
    .D12(_12_nibble_out[2]), .D13(_13_nibble_out[2]), .D14(_14_nibble_out[2]), .D15(_15_nibble_out[2]),
    .A0(Address[0]), .A1(Address[1]), .A2(Address[2]), .A3(Address[3]), .out_21(RAM_OUT[2]));
  and _1_3 (_1_3_out, Read_Write, new_decoder_1_y1);
  and _2_3 (_2_3_out, Read_Write, new_decoder_1_y2);
  // Probe on RAM_OUT
  and _3_2 (_3_2_out, Read_Write, new_decoder_1_y3);
  and _8_2 (_8_2_out, Read_Write, new_decoder_1_y8);
  and _9_2 (_9_2_out, Read_Write, new_decoder_1_y9);
  and _10_2 (_10_2_out, Read_Write, new_decoder_1_y10);
  and _11_2 (_11_2_out, Read_Write, new_decoder_1_y11);
  and _4_2 (_4_2_out, new_decoder_1_y4, Read_Write);
  and _5_2 (_5_2_out, Read_Write, new_decoder_1_y5);
  and _6_2 (_6_2_out, Read_Write, new_decoder_1_y6);
  and _7_2 (_7_2_out, Read_Write, new_decoder_1_y7);
  and _12_2 (_12_2_out, Read_Write, new_decoder_1_y12);
  and _13_2 (_13_2_out, Read_Write, new_decoder_1_y13);
  and _14_2 (_14_2_out, Read_Write, new_decoder_1_y14);
  and _15_2 (_15_2_out, Read_Write, new_decoder_1_y15);
  _16_to_1_mux _3_3 (
    .D0(_0_nibble_out[3]), .D1(_1_nibble_out[3]), .D2(_2_nibble_out[3]), .D3(_3_nibble_out[3]),
    .D4(_4_nibble_out[3]), .D5(_5_nibble_out[3]), .D6(_6_nibble_out[3]), .D7(_7_nibble_out[3]),
    .D8(_8_nibble_out[3]), .D9(_9_nibble_out[3]), .D10(_10_nibble_out[3]), .D11(_11_nibble_out[3]),
    .D12(_12_nibble_out[3]), .D13(_13_nibble_out[3]), .D14(_14_nibble_out[3]), .D15(_15_nibble_out[3]),
    .A0(Address[0]), .A1(Address[1]), .A2(Address[2]), .A3(Address[3]), .out_21(RAM_OUT[3]));

  // Notes on the sheet:
  //   Ken Li 260823059
  //   When Read_Write = 0 performs read, otherwise performs write
  //   MAKE SURE THAT YOU OPEN THIS PROJECT IN "LOGISIM-EVOLUTION"
endmodule

module Nibble (
  input  [3:0] Data,
  input  Read_Write,
  input  Enable,
  input  Clk,
  output [3:0] Nibble_Out
);

  wire and_1_out;

  // Probe on Data
  D_Flip_Flop d_ff_1 (
    .clk(Clk), .D(Data[0]), .Q(Nibble_Out[0]), .preset(1'b0), .en(and_1_out), .reset(1'b0));  // open: Qn
  D_Flip_Flop d_ff_2 (
    .clk(Clk), .D(Data[1]), .Q(Nibble_Out[1]), .preset(1'b0), .en(and_1_out), .reset(1'b0));  // open: Qn
  D_Flip_Flop d_ff_3 (
    .clk(Clk), .D(Data[2]), .Q(Nibble_Out[2]), .preset(1'b0), .en(and_1_out), .reset(1'b0));  // open: Qn
  D_Flip_Flop d_ff_4 (
    .clk(Clk), .D(Data[3]), .Q(Nibble_Out[3]), .preset(1'b0), .en(and_1_out), .reset(1'b0));  // open: Qn
  and and_1 (and_1_out, Enable, Read_Write);
  // Probe on Nibble_Out

  // Notes on the sheet:
  //   Ken Li 260823059
  //   When Read_Write = 0 performs read, otherwise performs write
  //   MAKE SURE THAT YOU OPEN THIS PROJECT IN "LOGISIM-EVOLUTION"
endmodule

// self build decoder
module New_decoder (
  input  A,
  input  B,
  input  C,
  input  D,
  output Y0,
  output Y1,
  output Y2,
  output Y3,
  output Y4,
  output Y5,
  output Y6,
  output Y7,
  output Y8,
  output Y9,
  output Y10,
  output Y11,
  output Y12,
  output Y13,
  output Y14,
  output Y15
);

  wire not_2_out, not_3_out, not_4_out, not_5_out, not_6_out, not_7_out, not_8_out, not_9_out, not_10_out,
       not_11_out, not_12_out, not_13_out, not_14_out, not_15_out, not_16_out, not_17_out, not_18_out,
       not_19_out, not_20_out, not_21_out, not_22_out, not_23_out, not_24_out, not_25_out, not_26_out,
       not_27_out, not_28_out, not_29_out, not_30_out, not_31_out, not_32_out, not_33_out, or_1_out,
       or_2_out, or_3_out, or_4_out, or_5_out, or_6_out, or_7_out, or_8_out, or_9_out, or_10_out, or_11_out,
       or_12_out, or_13_out, or_14_out, or_15_out, or_16_out;

  not not_1 (Y0, or_1_out);
  or or_1 (or_1_out, D, C, B, A);
  not not_2 (not_2_out, D);
  not not_3 (not_3_out, C);
  not not_4 (not_4_out, C);
  not not_5 (not_5_out, D);
  not not_6 (not_6_out, B);
  or or_2 (or_2_out, A, not_6_out, D, C);
  not not_7 (not_7_out, B);
  or or_3 (or_3_out, A, not_7_out, not_8_out, C);
  not not_8 (not_8_out, D);
  not not_9 (not_9_out, B);
  not not_10 (not_10_out, C);
  not not_11 (not_11_out, B);
  or or_4 (or_4_out, A, not_11_out, not_12_out, not_13_out);
  not not_12 (not_12_out, C);
  not not_13 (not_13_out, D);
  not not_14 (not_14_out, A);
  or or_5 (or_5_out, not_14_out, B, D, C);
  not not_15 (not_15_out, A);
  or or_6 (or_6_out, not_15_out, B, not_16_out, C);
  not not_16 (not_16_out, D);
  not not_17 (not_17_out, A);
  or or_7 (or_7_out, not_17_out, B, not_18_out, D);
  not not_18 (not_18_out, C);
  not not_19 (not_19_out, A);
  or or_8 (or_8_out, not_19_out, B, not_20_out, not_21_out);
  not not_20 (not_20_out, C);
  not not_21 (not_21_out, D);
  not not_22 (not_22_out, A);
  or or_9 (or_9_out, not_22_out, not_23_out, C, D);
  not not_23 (not_23_out, B);
  not not_24 (not_24_out, A);
  not not_25 (not_25_out, B);
  or or_10 (or_10_out, not_24_out, not_25_out, C, not_26_out);
  not not_26 (not_26_out, D);
  not not_27 (not_27_out, A);
  not not_28 (not_28_out, B);
  or or_11 (or_11_out, not_27_out, not_28_out, not_29_out, D);
  not not_29 (not_29_out, C);
  not not_30 (not_30_out, A);
  or or_12 (or_12_out, not_30_out, not_31_out, not_32_out, not_33_out);
  not not_31 (not_31_out, B);
  not not_32 (not_32_out, C);
  not not_33 (not_33_out, D);
  not not_34 (Y1, or_13_out);
  or or_13 (or_13_out, not_2_out, C, B, A);
  not not_35 (Y2, or_14_out);
  or or_14 (or_14_out, not_3_out, D, B, A);
  or or_15 (or_15_out, not_4_out, not_5_out, B, A);
  not not_36 (Y3, or_15_out);
  not not_37 (Y4, or_2_out);
  not not_38 (Y5, or_3_out);
  or or_16 (or_16_out, A, not_9_out, not_10_out, D);
  not not_39 (Y6, or_16_out);
  not not_40 (Y7, or_4_out);
  not not_41 (Y8, or_5_out);
  not not_42 (Y9, or_6_out);
  not not_43 (Y10, or_7_out);
  not not_44 (Y11, or_8_out);
  not not_45 (Y12, or_9_out);
  not not_46 (Y13, or_10_out);
  not not_47 (Y14, or_11_out);
  not not_48 (Y15, or_12_out);

  // Notes on the sheet:
  //   Ken Li 260823059
endmodule

module _8_to_1_Mux (
  input  D0,
  input  D1,
  input  D2,
  input  D3,
  input  D4,
  input  D5,
  input  D6,
  input  D7,
  input  a,
  input  b,
  input  c,
  output Out
);

  wire and_1_out, and_2_out, and_3_out, and_4_out, and_5_out, and_6_out, and_7_out, and_8_out, not_1_out,
       not_2_out, not_3_out;

  not not_1 (not_1_out, a);
  not not_2 (not_2_out, b);
  not not_3 (not_3_out, c);
  and and_1 (and_1_out, D0, not_1_out, not_2_out, not_3_out);
  and and_2 (and_2_out, D1, not_1_out, not_2_out, c);
  and and_3 (and_3_out, D2, not_1_out, not_3_out, b);
  and and_4 (and_4_out, D3, not_1_out, b, c);
  and and_5 (and_5_out, D4, a, not_2_out, not_3_out);
  and and_6 (and_6_out, D5, a, not_2_out, c);
  and and_7 (and_7_out, D6, a, b, not_3_out);
  and and_8 (and_8_out, D7, a, b, c);
  or or_1 (Out, and_1_out, and_2_out, and_3_out, and_4_out, and_5_out, and_6_out, and_7_out, and_8_out);

  // Notes on the sheet:
  //   Ken Li 260823059
endmodule

// self build mux0
module _16_to_1_mux (
  input  D0,
  input  D1,
  input  D2,
  input  D3,
  input  D4,
  input  D5,
  input  D6,
  input  D7,
  input  D8,
  input  D9,
  input  D10,
  input  D11,
  input  D12,
  input  D13,
  input  D14,
  input  D15,
  input  A0,
  input  A1,
  input  A2,
  input  A3,
  output out_21
);

  wire and_1_out, and_2_out, n8_to_1_mux_1_out, n8_to_1_mux_2_out, not_1_out;

  _8_to_1_Mux u_8_to_1_mux_1 (
    .D0(D8), .D1(D12), .D2(D10), .D3(D14), .D4(D9), .D5(D13), .D6(D11), .D7(D15), .a(A0), .b(A1), .c(A2),
    .Out(n8_to_1_mux_1_out));
  _8_to_1_Mux u_8_to_1_mux_2 (
    .D0(D0), .D1(D4), .D2(D2), .D3(D6), .D4(D1), .D5(D5), .D6(D3), .D7(D7), .a(A0), .b(A1), .c(A2),
    .Out(n8_to_1_mux_2_out));
  not not_1 (not_1_out, A3);
  and and_1 (and_1_out, n8_to_1_mux_2_out, not_1_out);
  and and_2 (and_2_out, n8_to_1_mux_1_out, A3);
  or or_1 (out_21, and_1_out, and_2_out);

  // Notes on the sheet:
  //   Ken Li 260823059
endmodule
